// Logisim project MainFile.circ as structural Verilog: 6 circuits, main circuit DN3
module DN3 (
  input  x1,
  input  x2,
  input  x3,
  input  x4,
  output f
);

  wire and_1_out, and_2_out, not_1_out, not_2_out, not_3_out, not_4_out, not_5_out, or_1_out, or_2_out,
       or_3_out, symmetry_4b_0_1_f, symmetry_4b_1_1_f, symmetry_4b_1_2_f, symmetry_4b_2_1_f, xor_1_out;

  not not_1 (not_1_out, x1);
  not not_2 (not_2_out, x2);
  not not_3 (not_3_out, x3);
  not not_4 (not_4_out, x4);
  xor xor_1 (xor_1_out, x1, x4);
  not not_5 (not_5_out, xor_1_out);
  or or_1 (or_1_out, not_1_out, not_3_out);
  Symmetry_4b_0 symmetry_4b_0_1 (.x1(x1), .x2(x2), .x3(x3), .x4(x4), .f(symmetry_4b_0_1_f));
  Symmetry_4b_1 symmetry_4b_1_1 (.x1(x1), .x2(x2), .x3(x3), .x4(x4), .f(symmetry_4b_1_1_f));
  Symmetry_4b_1 symmetry_4b_1_2 (.x1(not_1_out), .x2(x2), .x3(not_3_out), .x4(x4), .f(symmetry_4b_1_2_f));
  Symmetry_4b_2 symmetry_4b_2_1 (.x1(not_1_out), .x2(not_2_out), .x3(x3), .x4(x4), .f(symmetry_4b_2_1_f));
  or or_2 (or_2_out, symmetry_4b_0_1_f, symmetry_4b_1_1_f);
  and and_1 (and_1_out, or_1_out, symmetry_4b_2_1_f);
  or or_3 (or_3_out, or_2_out, symmetry_4b_1_2_f);
  and and_2 (and_2_out, not_5_out, or_3_out);
  or or_4 (f, and_2_out, and_1_out);
endmodule

module Symmetry_4b_0 (
  input  x1,
  input  x2,
  input  x3,
  input  x4,
  output f
);

  nor nor_1 (f, x1, x2, x3, x4);
endmodule

module Symmetry_4b_1 (
  input  x1,
  input  x2,
  input  x3,
  input  x4,
  output f
);

  ExactlyOne xor_1 (.out(f), .in0(x1), .in1(x2), .in2(x3), .in3(x4));
endmodule

module Symmetry_4b_2 (
  input  x1,
  input  x2,
  input  x3,
  input  x4,
  output f
);

  wire symmetry_4b_0_1_f, symmetry_4b_1_1_f, symmetry_4b_3_1_f, symmetry_4b_4_1_f;

  Symmetry_4b_0 symmetry_4b_0_1 (.x1(x1), .x2(x2), .x3(x3), .x4(x4), .f(symmetry_4b_0_1_f));
  Symmetry_4b_1 symmetry_4b_1_1 (.x1(x1), .x2(x2), .x3(x3), .x4(x4), .f(symmetry_4b_1_1_f));
  Symmetry_4b_3 symmetry_4b_3_1 (.x1(x1), .x2(x2), .x3(x3), .x4(x4), .f(symmetry_4b_3_1_f));
  Symmetry_4b_4 symmetry_4b_4_1 (.x1(x1), .x2(x2), .x3(x3), .x4(x4), .f(symmetry_4b_4_1_f));
  nor nor_1 (f, symmetry_4b_0_1_f, symmetry_4b_1_1_f, symmetry_4b_3_1_f, symmetry_4b_4_1_f);
endmodule

module Symmetry_4b_3 (
  input  x1,
  input  x2,
  input  x3,
  input  x4,
  output f
);

  ExactlyOne xor_1 (.out(f), .in0(x1), .in1(x2), .in2(x3), .in3(x4));
endmodule

module Symmetry_4b_4 (
  input  x1,
  input  x2,
  input  x3,
  input  x4,
  output f
);

  and and_1 (f, x1, x2, x3, x4);
endmodule
