// Logisim project Vaje10.circ as structural Verilog: 8 circuits, main circuit Main
module Symmetry_4b_0 (
  input  x1,
  input  x2,
  input  x3,
  input  x4,
  output f
);

  nor nor_1 (f, x1, x2, x3, x4);
endmodule

module Symmetry_4b_1 (
  input  x1,
  input  x2,
  input  x3,
  input  x4,
  output f
);

  ExactlyOne xor_1 (.out(f), .in0(x1), .in1(x2), .in2(x3), .in3(x4));
endmodule

module Symmetry_4b_2 (
  input  x1,
  input  x2,
  input  x3,
  input  x4,
  output f
);

  wire symmetry_4b_0_1_f, symmetry_4b_1_1_f, symmetry_4b_3_1_f, symmetry_4b_4_1_f;

  Symmetry_4b_0 symmetry_4b_0_1 (.x1(x1), .x2(x2), .x3(x3), .x4(x4), .f(symmetry_4b_0_1_f));
  Symmetry_4b_1 symmetry_4b_1_1 (.x1(x1), .x2(x2), .x3(x3), .x4(x4), .f(symmetry_4b_1_1_f));
  Symmetry_4b_3 symmetry_4b_3_1 (.x1(x1), .x2(x2), .x3(x3), .x4(x4), .f(symmetry_4b_3_1_f));
  Symmetry_4b_4 symmetry_4b_4_1 (.x1(x1), .x2(x2), .x3(x3), .x4(x4), .f(symmetry_4b_4_1_f));
  nor nor_1 (f, symmetry_4b_0_1_f, symmetry_4b_1_1_f, symmetry_4b_3_1_f, symmetry_4b_4_1_f);
endmodule

module Symmetry_4b_3 (
  input  x1,
  input  x2,
  input  x3,
  input  x4,
  output f
);

  ExactlyOne xor_1 (.out(f), .in0(x1), .in1(x2), .in2(x3), .in3(x4));
endmodule

module Symmetry_4b_4 (
  input  x1,
  input  x2,
  input  x3,
  input  x4,
  output f
);

  and and_1 (f, x1, x2, x3, x4);
endmodule

module Main (
  input  x
);

  wire clock_1_out, q1_q, q1_qn, q2_q, q2_qn, t1_1_t, t2_1_t;
  wire [1:0] y2_out;

  T_Flip_Flop q1 (.T(t1_1_t), .clk(clock_1_out), .Q(q1_q), .Qn(q1_qn));  // open: reset, preset
  t1 t1_1 (.q1(q1_q), .q2(q2_q), .x(x), .t(t1_1_t));
  T_Flip_Flop q2 (.T(t2_1_t), .clk(clock_1_out), .Q(q2_q), .Qn(q2_qn));  // open: reset, preset
  t2 t2_1 (.q1(q1_q), .q2(q2_q), .x(x), .t(t2_1_t));
  Clock clock_1 (.out(clock_1_out));
  and y1 (y2_out[1], q1_q, q2_qn);
  and y2 (y2_out[0], q1_qn, q2_q);
  Hex_Digit_Display hex_digit_display_1 (.value({2'b00, y2_out}));  // open: dp
endmodule

module t1 (
  input  q1,
  input  q2,
  input  x,
  output t
);

  wire and_1_out, and_2_out, and_3_out;

  and and_1 (and_1_out, q2, q1);
  and and_2 (and_2_out, ~q2, ~q1);  // AND_Gate
  and and_3 (and_3_out, ~x, ~q2);  // AND_Gate
  or or_1 (t, and_1_out, and_2_out, and_3_out);
endmodule

module t2 (
  input  q1,
  input  q2,
  input  x,
  output t
);

  wire and_1_out, and_2_out, and_3_out;

  and and_1 (and_1_out, ~q2, q1);  // AND_Gate
  and and_2 (and_2_out, ~q2, x);  // AND_Gate
  and and_3 (and_3_out, q2, ~x);  // AND_Gate
  or or_1 (t, and_1_out, and_2_out, and_3_out);
endmodule
